// Logisim project main.circ as structural Verilog: 3 circuits, main circuit main
module main (
  input  in_1
);

  wire controlador_auto_1_out_2, controlador_auto_1_out_3, controlador_auto_1_out_4,
       controlador_peaton_1_out_2, controlador_peaton_1_out_3, not_1_out, or_1_out, or_2_out, or_3_out,
       or_4_out, or_5_out;

  not not_1 (not_1_out, in_1);
  controlador_auto controlador_auto_1 (
    .in_1(not_1_out), .out_2(controlador_auto_1_out_2), .out_3(controlador_auto_1_out_3),
    .out_4(controlador_auto_1_out_4));
  controlador_peaton controlador_peaton_1 (
    .in_1(not_1_out), .out_2(controlador_peaton_1_out_2), .out_3(controlador_peaton_1_out_3));
  or or_1 (or_1_out, in_1, controlador_auto_1_out_2);
  or or_2 (or_2_out, in_1, controlador_auto_1_out_3);
  or or_3 (or_3_out, in_1, controlador_auto_1_out_4);
  or or_4 (or_4_out, in_1, controlador_peaton_1_out_2);
  or or_5 (or_5_out, in_1, controlador_peaton_1_out_3);
  LED led_1 (.in(or_1_out));
  LED led_2 (.in(or_2_out));
  LED led_3 (.in(or_3_out));
  LED led_4 (.in(or_4_out));
  LED led_5 (.in(or_5_out));

  // Notes on the sheet:
  //   el circuito
  //   ROJO AUTO
  //   AMARILLO AUTO
  //   VERDE AUTO
  //   ROJO PEATON
  //   VERDE PEATON
endmodule

// auto
module controlador_auto (
  input  in_1,
  output out_2,
  output out_3,
  output out_4
);

  not not_1 (out_2, in_1);
  not not_2 (out_3, in_1);

  assign out_4 = in_1;
endmodule

// peaton
module controlador_peaton (
  input  in_1,
  output out_2,
  output out_3
);

  not not_1 (out_3, in_1);

  assign out_2 = in_1;
endmodule
